# Fritzing sketch ir (saved by Fritzing 0.9.3b)
breadboards: 1

parts:
  IR1 = TSOP312.., 314.. [package=THT]
  Part2 = Arduino Uno (Rev3)
  BAT1 = BC9VPC [package=bc9vpc]  # not connected

nets:
  GND: IR1.GND, Part2.GND
  N1: IR1.Vs, Part2.5V
  N2: IR1.Data, Part2.D12/MISO
