# Fritzing sketch distance (saved by Fritzing 0.9.3b)
breadboards: 1

parts:
  hc-sr1 = hc-sr04
  Part2 = Arduino Uno (Rev3)
  BAT1 = BC9VPC [package=bc9vpc]  # not connected

nets:
  VCC: hc-sr1.VCC, Part2.5V
  N1: hc-sr1.Trig, Part2.D2
  N2: hc-sr1.Echo, Part2.D4
  GND: hc-sr1.GND, Part2.GND
