# Fritzing sketch motor (saved by Fritzing 0.9.3b)
breadboards: 1

parts:
  Part2 = Arduino Uno (Rev3)
  J1 = Basic Servo
  BAT1 = BC9VPC [package=bc9vpc]  # not connected

nets:
  N1: Part2.D8, J1.pulse
  5V: Part2.5V, J1.vcc
  GND: Part2.GND, J1.gnd
